// Logisim project 洗衣机.circ as structural Verilog: 15 circuits, main circuit 洗衣机
module \洗衣机  (
);

  wire BeepLED, Children, CLK, Mode, Power, PowerLED, Rinse, Spin, SPLED, StartPause, Wash;
  wire [3:0] one, one1, one2, ten, ten1, ten2;

  Clock #(.highDuration(1), .lowDuration(1)) clock_1 (.out(CLK));
  _7_Segment_Display #(.active("true")) u_7_segment_display_1 (
    .g(ten1[3]), .f(ten1[2]), .a(ten1[1]), .b(ten1[0]), .e(ten2[3]), .d(ten2[2]), .c(ten2[1]), .dp(ten2[0]));
  _7_Segment_Display #(.active("true")) u_7_segment_display_2 (
    .g(one1[3]), .f(one1[2]), .a(one1[1]), .b(one1[0]), .e(one2[3]), .d(one2[2]), .c(one2[1]), .dp(one2[0]));
  LED #(.active("true")) led_1 (.in(Wash));
  LED #(.active("true")) led_2 (.in(Rinse));
  LED #(.active("true")) led_3 (.in(Spin));
  \洗衣机控制电路  \u_洗衣机控制电路_1  (
    .in_1(StartPause), .in_2(Mode), .POWER(PowerLED), .\洗衣指示灯 (Wash), .out_8(ten), .\漂洗指示灯 (Rinse),
    .out_10(one), .\甩干指示灯 (Spin), .\启动_暂停指示灯 (SPLED), .out_13(BeepLED), .refresh(Power), .CLK(CLK),
    .in_5(Children));
  // Buzzer #(.freq_measure("Hz"), .vol_width(7)) buzzer_1: pin names not known; wires that end beside it: ten, BeepLED
  Button button_1 (.out(Power));
  Button button_2 (.out(StartPause));
  Button button_3 (.out(Mode));
  Button button_4 (.out(Children));
  \数码管驱动  \u_数码管驱动_1  (.out_4(ten1), .out_5(ten2), .in_1(ten), .in_2(one), .out_6(one1), .out_7(one2), .EN(PowerLED));
  LED #(.active("true")) led_4 (.in(PowerLED));
  LED #(.active("true")) led_5 (.in(BeepLED));
  LED #(.active("true")) led_6 (.in(SPLED));
  Power power_1 (.in_1(Power), .out_2(PowerLED));

  // Notes on the sheet:
  //   洗衣指示灯
  //   漂洗指示灯
  //   甩干指示灯
  //   注意：遇到打开电源后显示00，按按钮无反应等情况，记得按Ctrl+K打开时钟
  //   华中科技大学数字逻辑与电路设计实验课作业
  //   2021.12.6
  //   电源指示灯
  //   蜂鸣指示灯
  //   启动/暂停指示灯
endmodule

module \_7段数码管显示译码电路  (
  input  X3,
  input  X2,
  input  X1,
  input  X0,
  output S1,
  output S2,
  output S3,
  output S4,
  output x,
  output S6,
  output S7
);

  wire and_1_out, and_2_out, and_3_out, and_4_out, and_5_out, and_6_out, and_7_out, and_8_out, and_9_out,
       and_10_out, and_11_out, and_12_out, and_13_out, and_14_out, and_15_out, and_16_out, and_17_out,
       not_1_out, not_2_out, not_3_out, not_4_out, not_5_out, not_6_out, not_7_out, not_8_out, not_9_out,
       not_10_out, not_11_out, not_12_out, not_13_out, not_14_out, not_15_out, not_16_out, not_17_out,
       not_18_out, not_19_out, not_20_out, not_21_out, not_22_out, not_23_out;

  not not_1 (not_1_out, X3);
  not not_2 (not_2_out, X2);
  and and_1 (and_1_out, not_1_out, not_2_out, X1);
  and and_2 (and_2_out, X2, not_3_out);
  not not_3 (not_3_out, X1);
  and and_3 (and_3_out, X2, not_4_out);
  not not_4 (not_4_out, X0);
  and and_4 (and_4_out, X3, not_5_out);
  not not_5 (not_5_out, X1);
  not not_6 (not_6_out, X1);
  and and_5 (and_5_out, not_6_out, not_7_out);
  not not_7 (not_7_out, X0);
  and and_6 (and_6_out, X2, not_8_out);
  not not_8 (not_8_out, X1);
  and and_7 (and_7_out, X2, not_9_out);
  not not_9 (not_9_out, X0);
  not not_10 (not_10_out, X2);
  and and_8 (and_8_out, not_10_out, not_11_out);
  not not_11 (not_11_out, X0);
  and and_9 (and_9_out, X2, X0);
  not not_12 (not_12_out, X2);
  not not_13 (not_13_out, X1);
  and and_10 (and_10_out, not_13_out, not_14_out);
  not not_14 (not_14_out, X0);
  and and_11 (and_11_out, X1, X0);
  not not_15 (not_15_out, X2);
  and and_12 (and_12_out, not_15_out, not_16_out);
  not not_16 (not_16_out, X0);
  and and_13 (and_13_out, X1, not_17_out);
  not not_17 (not_17_out, X0);
  not not_18 (not_18_out, X2);
  and and_14 (and_14_out, not_18_out, not_19_out);
  not not_19 (not_19_out, X0);
  not not_20 (not_20_out, X2);
  and and_15 (and_15_out, not_20_out, X1);
  and and_16 (and_16_out, X1, not_21_out);
  not not_21 (not_21_out, X0);
  not not_22 (not_22_out, X1);
  and and_17 (and_17_out, X2, not_22_out, X0);
  not not_23 (not_23_out, X1);
  or or_1 (S1, and_1_out, and_2_out, and_3_out, and_4_out);
  or or_2 (S2, and_5_out, and_6_out, and_7_out, X3);
  or or_3 (S3, and_8_out, X1, and_9_out, X3);
  or or_4 (S4, not_12_out, and_10_out, and_11_out);
  or or_5 (x, and_12_out, and_13_out);
  or or_6 (S6, and_14_out, and_15_out, and_16_out, and_17_out, X3);
  or or_7 (S7, not_23_out, X0, X2, X3);
  // DisplayDecoder #(.multibit("true")) displaydecoder_1: pin names not known
  Hex_Digit_Display hex_digit_display_1 ();  // open: value, dp
endmodule

module \指示灯驱动  (
  input  in_1,
  input  in_2,
  input  in_3,
  input  in_4,
  input  in_5,
  output out_6,
  output out_7,
  output out_8,
  output out_9
);


  // Other names for the same wires on the sheet: clk = in_5; LED1 = out_6; LED2 = out_7; LED3 = out_8; LED4 = out_9;
  //   S = in_4; X1 = in_1; X2 = in_2; X3 = in_3
endmodule

module \蜂鸣器驱动  (
  input  in_1,
  input  in_2
);
endmodule

module \计时模块  (
  input  \开始 ,
  input  CLK,
  input  \暂停 ,
  input  \写入 ,
  input  [3:0] \十位 ,
  input  [3:0] \个位 ,
  output [3:0] \十位_2 ,
  output [3:0] \个位_2 
);

  wire and_1_out, and_2_out, and_3_out, counter_1_carry, counter_3_carry, d_ff_1_q, Minute,
       multiplexer_1_out, multiplexer_2_out, not_1_out, s_r_ff_1_q, t_ff_1_q;

  T_Flip_Flop #(.trigger("rising"), .Pre_Clr_Positions("ABOVE_BELOW"), .NegatePresetClear("false"), .enable("false"), .NewFFLayout("true")) t_ff_1 (
    .clk(\暂停 ), .T(1'b1), .Q(t_ff_1_q));  // open: Qn, preset, reset
  D_Flip_Flop #(.trigger("rising"), .Pre_Clr_Positions("ABOVE_BELOW"), .NegatePresetClear("false"), .enable("false"), .NewFFLayout("true")) d_ff_1 (
    .clk(CLK), .D(\写入 ), .Q(d_ff_1_q));  // open: Qn, preset, reset
  S_R_Flip_Flop #(.trigger("rising"), .Pre_Clr_Positions("ABOVE_BELOW"), .NegatePresetClear("false"), .enable("false"), .NewFFLayout("true")) s_r_ff_1 (
    .S(\开始 ), .clk(CLK), .R(and_3_out), .Q(s_r_ff_1_q));  // open: Qn, preset, reset
  and and_1 (and_1_out, s_r_ff_1_q, ~t_ff_1_q);  // AND_Gate
  Hex_Digit_Display hex_digit_display_1 (.value(\十位_2 ));  // open: dp
  Counter #(.width(4), .max('h9), .ongoal("wrap"), .trigger("rising"), .behavior("new")) counter_1 (
    .load(d_ff_1_q), .D(\十位 ), .Q(\十位_2 ), .carry(counter_1_carry), .clk(multiplexer_1_out), .down(1'b1));  // open: count, clr, preset
  Multiplexer #(.select(1), .width(1), .disabled("Z"), .enable("false")) multiplexer_1 (
    .in0(not_1_out), .in1(CLK), .out(multiplexer_1_out), .sel(d_ff_1_q));
  Counter #(.width(8), .max('h40), .ongoal("wrap"), .trigger("rising"), .behavior("new")) counter_2 (
    .count(and_1_out), .carry(Minute), .clk(CLK));  // open: load, D, Q, clr, preset, down
  and and_2 (and_2_out, ~counter_1_carry, counter_3_carry);  // AND_Gate
  not not_1 (not_1_out, and_2_out);
  Hex_Digit_Display hex_digit_display_2 (.value(\个位_2 ));  // open: dp
  Multiplexer #(.select(1), .width(1), .disabled("Z"), .enable("false")) multiplexer_2 (
    .in0(Minute), .in1(CLK), .out(multiplexer_2_out), .sel(d_ff_1_q));
  Counter #(.width(4), .max('h9), .ongoal("wrap"), .trigger("rising"), .behavior("new")) counter_3 (
    .load(d_ff_1_q), .D(\个位 ), .Q(\个位_2 ), .carry(counter_3_carry), .clk(multiplexer_2_out), .down(1'b1));  // open: count, clr, preset
  and and_3 (and_3_out, counter_3_carry, counter_1_carry);

  // Other names for the same wires on the sheet: CLKl = CLK

  // Notes on the sheet:
  //   去除险象
  //   本质就是一个计时器，断电的同时清零
  //   不加这个D触发器是，CLK=0时，写入从1变为0，十位减1
  //   此处的滴答数为一分钟的，也就是60*f（频率）
endmodule

module \数码管驱动  (
  input  [3:0] in_1,
  input  [3:0] in_2,
  input  EN,
  output [3:0] out_4,
  output [3:0] out_5,
  output [3:0] out_6,
  output [3:0] out_7
);

  wire displaydecoder_1_p2, displaydecoder_2_p2;

  // DisplayDecoder #(.multibit("true")) displaydecoder_1: pin names not known; wires that end beside it: in_1, displaydecoder_1_p2, displaydecoder_1_p2, EN, out_4[1], out_4[0], out_5[1], out_5[2], out_5[3], out_4[2], out_4[3]
  // DisplayDecoder #(.multibit("true")) displaydecoder_2: pin names not known; wires that end beside it: in_2, displaydecoder_2_p2, displaydecoder_2_p2, EN, out_6[1], out_6[0], out_7[1], out_7[2], out_7[3], out_6[2], out_6[3]

  assign out_5[0] = 1'b0;
  assign out_7[0] = 1'b0;
endmodule

module \洗衣机控制电路  (
  input  in_1,
  input  in_2,
  input  CLK,
  input  POWER,
  input  in_5,
  input  refresh,
  output \洗衣指示灯 ,
  output [3:0] out_8,
  output \漂洗指示灯 ,
  output [3:0] out_10,
  output \甩干指示灯 ,
  output \启动_暂停指示灯 ,
  output out_13
);

  wire and_1_out, and_2_out, and_4_out, and_5_out, and_8_out, and_9_out, Any1Beep, \beep_1__9声响铃结束 ,
       buzzer_1_p2, Choosing, Finish, Finish1, Finish2, Finish4, Finish5, Finish6, Mode, MODE1, MODE2, MODE3,
       MODE4, MODE5, MODE6, not_1_out, or_2_out, or_3_out, or_4_out, or_5_out, Pause, refresh_t, Rinse1,
       Rinse3, Rinse4, Rinse5, Spin1, Spin5, Spin6, Start, StartPause, t_ff_1_q, t_ff_2_qn, t_ff_3_qn, Wash1,
       Wash2, Wash3, \洗衣模块_1_out_5 , \洗衣模块_3_out_5 , \漂洗模块_2_out_5 , \漂洗模块_3_out_5 ;
  wire [3:0] one0, ten0;

  Hex_Digit_Display hex_digit_display_1 (.value(out_8));  // open: dp
  \洗衣流程控制  \u_洗衣流程控制_1  (
    .\置1 (refresh_t), .MODE(Mode), .\模式选择中 (Choosing), .out_4({MODE6, MODE5, MODE4, MODE3, MODE2, MODE1}),
    .out_5(ten0), .out_6(one0));
  Hex_Digit_Display hex_digit_display_2 (.value(out_10));  // open: dp
  and and_1 (and_1_out, ~refresh_t, MODE1);  // AND_Gate
  and and_2 (and_2_out, ~refresh_t, MODE4);  // AND_Gate
  \洗衣模块  \u_洗衣模块_1  (.EN(and_1_out), .\开始 (Start), .CLK(CLK), .\暂停 (Pause), .out_5(\洗衣模块_1_out_5 ), .\对应的灯 (Wash1));
  \漂洗模块  \u_漂洗模块_1  (.EN(and_2_out), .\开始 (Start), .out_5(Finish4), .CLK(CLK), .\对应的灯 (Rinse4), .\暂停 (Pause));
  T_Flip_Flop #(.trigger("falling"), .Pre_Clr_Positions("ABOVE_BELOW"), .NegatePresetClear("false"), .enable("false"), .NewFFLayout("true")) t_ff_1 (
    .clk(Start), .T(1'b1), .Q(t_ff_1_q), .Qn(Choosing), .reset(refresh_t));  // open: preset
  \漂洗模块  \u_漂洗模块_2  (
    .EN(and_1_out), .\开始 (\洗衣模块_1_out_5 ), .out_5(\漂洗模块_2_out_5 ), .CLK(CLK), .\对应的灯 (Rinse1), .\暂停 (Pause));
  Demultiplexer #(.select(1), .width(1), .tristate("false"), .disabled("Z"), .enable("false")) demultiplexer_1 (
    .out0(Start), .out1(Pause), .in(StartPause), .sel(t_ff_1_q));
  \甩干模块  \u_甩干模块_1  (.EN(and_1_out), .\开始 (\漂洗模块_2_out_5 ), .out_5(Finish1), .CLK(CLK), .\对应的灯 (Spin1), .\暂停 (Pause));
  and and_3 (\启动_暂停指示灯 , t_ff_1_q, POWER, t_ff_2_qn);
  T_Flip_Flop #(.trigger("falling"), .Pre_Clr_Positions("ABOVE_BELOW"), .NegatePresetClear("false"), .enable("false"), .NewFFLayout("true")) t_ff_2 (
    .clk(Pause), .T(1'b1), .Qn(t_ff_2_qn));  // open: Q, preset, reset
  and and_4 (and_4_out, ~refresh_t, MODE5);  // AND_Gate
  \漂洗模块  \u_漂洗模块_3  (.EN(and_4_out), .\开始 (Start), .out_5(\漂洗模块_3_out_5 ), .CLK(CLK), .\对应的灯 (Rinse5), .\暂停 (Pause));
  or or_1 (refresh_t, refresh, \beep_1__9声响铃结束 );
  Beep beep_1 (.CLK(CLK), .Beep(Any1Beep), .out_6(out_13), .Beep9(Finish), .EN(POWER), .\_9声响铃结束 (\beep_1__9声响铃结束 ));
  // Buzzer #(.freq_measure("Hz"), .vol_width(7)) buzzer_1: pin names not known; wires that end beside it: out_13, buzzer_1_p2, buzzer_1_p2
  \甩干模块  \u_甩干模块_2  (.EN(and_4_out), .\开始 (\漂洗模块_3_out_5 ), .out_5(Finish5), .CLK(CLK), .\对应的灯 (Spin5), .\暂停 (Pause));
  and and_5 (and_5_out, ~refresh_t, MODE2);  // AND_Gate
  T_Flip_Flop #(.trigger("rising"), .Pre_Clr_Positions("ABOVE_BELOW"), .NegatePresetClear("false"), .enable("false"), .NewFFLayout("true")) t_ff_3 (
    .clk(in_5), .T(1'b1), .Qn(t_ff_3_qn), .reset(not_1_out));  // open: Q, preset
  not not_1 (not_1_out, POWER);
  \洗衣模块  \u_洗衣模块_2  (.EN(and_5_out), .\开始 (Start), .CLK(CLK), .\暂停 (Pause), .out_5(Finish2), .\对应的灯 (Wash2));
  and and_6 (StartPause, t_ff_3_qn, in_1);
  and and_7 (Mode, t_ff_3_qn, in_2);
  \计时模块  \u_计时模块_1  (
    .\开始 (Start), .CLK(CLK), .\暂停 (Pause), .\写入 (Choosing), .\十位 (ten0), .\个位 (one0), .\十位_2 (out_8),
    .\个位_2 (out_10));
  and and_8 (and_8_out, ~refresh_t, MODE6);  // AND_Gate
  \甩干模块  \u_甩干模块_3  (.EN(and_8_out), .\开始 (Start), .out_5(Finish6), .CLK(CLK), .\对应的灯 (Spin6), .\暂停 (Pause));
  and and_9 (and_9_out, ~refresh_t, MODE3);  // AND_Gate
  or or_2 (or_2_out, StartPause, Mode);
  or or_3 (or_3_out, Wash1, Wash2, Wash3);
  or or_4 (or_4_out, Rinse1, Rinse3, Rinse4, Rinse5);
  or or_5 (or_5_out, Spin1, Spin5, Spin6);
  \洗衣模块  \u_洗衣模块_3  (.EN(and_9_out), .\开始 (Start), .CLK(CLK), .\暂停 (Pause), .out_5(\洗衣模块_3_out_5 ), .\对应的灯 (Wash3));
  and and_10 (Any1Beep, POWER, or_2_out);
  and and_11 (\洗衣指示灯 , POWER, or_3_out);
  and and_12 (\漂洗指示灯 , POWER, or_4_out);
  and and_13 (\甩干指示灯 , POWER, or_5_out);
  \漂洗模块  \u_漂洗模块_4  (.EN(and_9_out), .\开始 (\洗衣模块_3_out_5 ), .out_5(Finish2), .CLK(CLK), .\对应的灯 (Rinse3), .\暂停 (Pause));
  or or_6 (Finish, Finish1, Finish2, Finish2, Finish4, Finish5, Finish6);

  // Other names for the same wires on the sheet: BeepLED = out_13; Children = in_5; EN = POWER; Finish3 = Finish2;
  //   Mode0 = in_2; one[3:0] = out_10; Rinse = \漂洗指示灯 ; Spin = \甩干指示灯 ; SPLED = \启动_暂停指示灯 ; StartPause0 = in_1;
  //   ten[3:0] = out_8; Wash = \洗衣指示灯 

  // Notes on the sheet:
  //   流程情况1
  //   流程情况4
  //   模式选择
  //   开始逻辑
  //   流程情况5
  //   流程结束逻辑
  //   流程情况2
  //   电源指示灯
  //   蜂鸣指示灯
  //   显示初值写入
  //   流程情况6
  //   流程情况3
  //   一分钟暂时用2秒代替
endmodule

module Power (
  input  in_1,
  output out_2
);

  T_Flip_Flop #(.trigger("rising"), .Pre_Clr_Positions("ABOVE_BELOW"), .NegatePresetClear("false"), .enable("false"), .NewFFLayout("true")) t_ff_1 (
    .clk(in_1), .T(1'b1), .Q(out_2));  // open: Qn, preset, reset
endmodule

module \洗衣流程控制组合电路  (
  input  S2,
  input  S1,
  input  S0,
  output N2,
  output N1,
  output N0
);

  wire and_1_out, and_2_out, and_3_out, and_4_out, and_5_out, and_6_out, and_7_out, and_8_out, and_9_out,
       and_10_out, not_1_out, not_2_out, not_3_out, not_4_out, not_5_out, not_6_out, not_7_out, not_8_out,
       not_9_out, not_10_out, not_11_out, not_12_out, not_13_out, not_14_out, not_15_out, not_16_out;

  and and_1 (and_1_out, S2, S1, S0);
  not not_1 (not_1_out, S1);
  and and_2 (and_2_out, S2, not_1_out, not_2_out);
  not not_2 (not_2_out, S0);
  not not_3 (not_3_out, S2);
  not not_4 (not_4_out, S1);
  and and_3 (and_3_out, not_3_out, not_4_out, S0);
  and and_4 (and_4_out, S2, not_5_out, not_6_out);
  not not_5 (not_5_out, S1);
  not not_6 (not_6_out, S0);
  and and_5 (and_5_out, S2, S1, not_7_out);
  not not_7 (not_7_out, S0);
  not not_8 (not_8_out, S2);
  and and_6 (and_6_out, not_8_out, S1, not_9_out);
  not not_9 (not_9_out, S0);
  not not_10 (not_10_out, S2);
  not not_11 (not_11_out, S1);
  and and_7 (and_7_out, not_10_out, not_11_out, S0);
  not not_12 (not_12_out, S2);
  and and_8 (and_8_out, not_12_out, S1, not_13_out);
  not not_13 (not_13_out, S0);
  not not_14 (not_14_out, S2);
  and and_9 (and_9_out, not_14_out, S1, S0);
  not not_15 (not_15_out, S2);
  and and_10 (and_10_out, not_15_out, not_16_out, S0);
  not not_16 (not_16_out, S1);
  or or_1 (N2, and_1_out, and_2_out, and_3_out);
  or or_2 (N1, and_4_out, and_5_out, and_6_out, and_7_out);
  or or_3 (N0, and_8_out, and_9_out, and_10_out);
endmodule

module \洗衣流程控制输出函数  (
  input  a,
  input  b,
  input  c,
  output x,
  output y,
  output z,
  output u,
  output v,
  output w
);

  wire not_1_out, not_2_out, not_3_out, not_4_out, not_5_out, not_6_out, not_7_out, not_8_out;

  and and_1 (x, a, b, c);
  not not_1 (not_1_out, b);
  not not_2 (not_2_out, c);
  not not_3 (not_3_out, c);
  not not_4 (not_4_out, a);
  not not_5 (not_5_out, c);
  not not_6 (not_6_out, a);
  not not_7 (not_7_out, a);
  not not_8 (not_8_out, b);
  and and_2 (y, a, not_1_out, not_2_out);
  and and_3 (z, a, b, not_3_out);
  and and_4 (u, not_4_out, b, not_5_out);
  and and_5 (v, not_6_out, b, c);
  and and_6 (w, not_7_out, not_8_out, c);
endmodule

module Beep (
  input  EN,
  input  CLK,
  input  Beep,
  input  Beep9,
  output \_9声响铃结束 ,
  output out_6
);

  wire and_1_out, and_2_out, and_3_out, and_4_out, Beep3, button_1_out, clock_1_out, counter_1_carry,
       counter_2_carry, counter_3_carry, counter_5_carry, counter_6_carry, d_ff_1_q, d_ff_2_q, not_1_out,
       not_2_out, or_1_out, or_2_out, s_r_ff_1_q, s_r_ff_3_q, s_r_ff_4_q, s_r_ff_5_q, s_r_ff_5_qn, t_ff_1_q,
       t_ff_1_qn, undriven, xor_1_out;

  Clock #(.highDuration(1), .lowDuration(1)) clock_1 (.out(clock_1_out));
  Button button_1 (.out(button_1_out));
  Button button_2 ();  // open: out
  D_Flip_Flop #(.trigger("rising"), .Pre_Clr_Positions("ABOVE_BELOW"), .NegatePresetClear("false"), .enable("false"), .NewFFLayout("true")) d_ff_1 (
    .clk(CLK), .D(Beep), .Q(d_ff_1_q));  // open: Qn, preset, reset
  S_R_Flip_Flop #(.trigger("rising"), .Pre_Clr_Positions("ABOVE_BELOW"), .NegatePresetClear("false"), .enable("false"), .NewFFLayout("true")) s_r_ff_1 (
    .S(and_1_out), .clk(CLK), .R(counter_1_carry), .Q(s_r_ff_1_q), .reset(button_1_out));  // open: Qn, preset
  D_Flip_Flop #(.trigger("rising"), .Pre_Clr_Positions("ABOVE_BELOW"), .NegatePresetClear("false"), .enable("false"), .NewFFLayout("true")) d_ff_2 (
    .clk(CLK), .D(d_ff_1_q), .Q(d_ff_2_q));  // open: Qn, preset, reset
  Counter #(.width(8), .max('h6), .ongoal("wrap"), .trigger("rising"), .behavior("new")) counter_1 (
    .count(s_r_ff_1_q), .carry(counter_1_carry), .clk(CLK), .clr(button_1_out));  // open: load, D, Q, preset, down
  or or_1 (or_1_out, Beep9, Beep3);
  S_R_Flip_Flop #(.trigger("high"), .Pre_Clr_Positions("ABOVE_BELOW"), .NegatePresetClear("false"), .enable("false"), .NewFFLayout("true")) s_r_ff_2 (
    .S(\_9声响铃结束 ), .clk(undriven), .R(1'b0));  // open: Q, Qn, preset, reset
  xor xor_1 (xor_1_out, d_ff_2_q, d_ff_1_q);
  S_R_Flip_Flop #(.trigger("rising"), .Pre_Clr_Positions("ABOVE_BELOW"), .NegatePresetClear("false"), .enable("false"), .NewFFLayout("true")) s_r_ff_3 (
    .S(Beep9), .clk(CLK), .R(counter_2_carry), .Q(s_r_ff_3_q), .reset(\_9声响铃结束 ));  // open: Qn, preset
  and and_1 (and_1_out, xor_1_out, d_ff_1_q);
  Counter #(.width(8), .max('h2), .ongoal("wrap"), .trigger("rising"), .behavior("new")) counter_2 (
    .count(s_r_ff_3_q), .carry(counter_2_carry), .clk(and_2_out), .clr(\_9声响铃结束 ));  // open: load, D, Q, preset, down
  and and_2 (and_2_out, ~s_r_ff_4_q, s_r_ff_5_q);  // AND_Gate
  not not_1 (not_1_out, counter_2_carry);
  S_R_Flip_Flop #(.trigger("rising"), .Pre_Clr_Positions("ABOVE_BELOW"), .NegatePresetClear("false"), .enable("false"), .NewFFLayout("true")) s_r_ff_4 (
    .S(or_1_out), .clk(CLK), .R(counter_3_carry), .Q(s_r_ff_4_q), .reset(and_2_out));  // open: Qn, preset
  Counter #(.width(8), .max('h3), .ongoal("wrap"), .trigger("rising"), .behavior("new")) counter_3 (
    .count(s_r_ff_4_q), .carry(counter_3_carry), .clk(counter_6_carry), .clr(and_2_out));  // open: load, D, Q, preset, down
  T_Flip_Flop #(.trigger("rising"), .Pre_Clr_Positions("ABOVE_BELOW"), .NegatePresetClear("false"), .enable("false"), .NewFFLayout("true")) t_ff_1 (
    .clk(and_2_out), .T(not_1_out), .Q(t_ff_1_q), .Qn(t_ff_1_qn), .reset(s_r_ff_4_q));  // open: preset
  Counter #(.width(8), .max('h10), .ongoal("wrap"), .trigger("rising"), .behavior("new")) counter_4 (
    .count(t_ff_1_q), .carry(Beep3), .clk(CLK), .clr(t_ff_1_qn));  // open: load, D, Q, preset, down
  S_R_Flip_Flop #(.trigger("rising"), .Pre_Clr_Positions("ABOVE_BELOW"), .NegatePresetClear("false"), .enable("false"), .NewFFLayout("true")) s_r_ff_5 (
    .S(or_2_out), .clk(CLK), .R(counter_5_carry), .Q(s_r_ff_5_q), .Qn(s_r_ff_5_qn), .reset(and_2_out));  // open: preset
  or or_2 (or_2_out, or_1_out, counter_6_carry);
  and and_3 (and_3_out, s_r_ff_4_q, s_r_ff_5_q);
  D_Flip_Flop #(.trigger("falling"), .Pre_Clr_Positions("ABOVE_BELOW"), .NegatePresetClear("false"), .enable("false"), .NewFFLayout("true")) d_ff_3 (
    .clk(s_r_ff_4_q), .D(1'b1), .Q(\_9声响铃结束 ), .reset(not_2_out));  // open: Qn, preset
  not not_2 (not_2_out, counter_2_carry);
  and and_4 (and_4_out, s_r_ff_4_q, s_r_ff_5_qn);
  Counter #(.width(8), .max('h4), .ongoal("wrap"), .trigger("rising"), .behavior("new")) counter_5 (
    .count(and_3_out), .carry(counter_5_carry), .clk(CLK), .clr(and_2_out));  // open: load, D, Q, preset, down
  Counter #(.width(8), .max('h10), .ongoal("wrap"), .trigger("rising"), .behavior("new")) counter_6 (
    .count(and_4_out), .carry(counter_6_carry), .clk(CLK), .clr(and_2_out));  // open: load, D, Q, preset, down
  or or_3 (out_6, s_r_ff_1_q, and_3_out);
  // Buzzer #(.freq_measure("Hz"), .vol_width(7)) buzzer_1: pin names not known

  // Other names for the same wires on the sheet: refresh = \_9声响铃结束 

  // Notes on the sheet:
  //   此信号需要用高电平触发才能捕获到
endmodule

module \洗衣模块  (
  input  EN,
  input  \开始 ,
  input  CLK,
  input  \暂停 ,
  output out_5,
  output \对应的灯 
);

  wire and_1_out, and_2_out, and_3_out, multiplexer_1_out, not_1_out, not_2_out, or_1_out,
       programmablegenerator_1_p1, s_r_ff_1_q, s_r_ff_2_qn, t_ff_1_q;

  T_Flip_Flop #(.trigger("rising"), .Pre_Clr_Positions("ABOVE_BELOW"), .NegatePresetClear("false"), .enable("false"), .NewFFLayout("true")) t_ff_1 (
    .clk(\暂停 ), .T(1'b1), .Q(t_ff_1_q), .reset(not_2_out));  // open: Qn, preset
  S_R_Flip_Flop #(.trigger("rising"), .Pre_Clr_Positions("ABOVE_BELOW"), .NegatePresetClear("false"), .enable("false"), .NewFFLayout("true")) s_r_ff_1 (
    .S(\开始 ), .clk(CLK), .R(out_5), .Q(s_r_ff_1_q), .reset(not_2_out));  // open: Qn, preset
  not not_1 (not_1_out, t_ff_1_q);
  not not_2 (not_2_out, EN);
  and and_1 (and_1_out, EN, s_r_ff_1_q, not_1_out);
  Counter #(.width(16), .max('h140), .ongoal("wrap"), .trigger("rising"), .behavior("new")) counter_1 (
    .count(and_1_out), .carry(out_5), .clk(CLK));  // open: load, D, Q, clr, preset, down
  and and_2 (and_2_out, t_ff_1_q, s_r_ff_1_q);
  // ProgrammableGenerator #(.nState(1), .Contents("10 10")) programmablegenerator_1: pin names not known; wires that end beside it: programmablegenerator_1_p1
  and and_3 (and_3_out, and_1_out, programmablegenerator_1_p1);
  S_R_Flip_Flop #(.trigger("rising"), .Pre_Clr_Positions("ABOVE_BELOW"), .NegatePresetClear("false"), .enable("false"), .NewFFLayout("true")) s_r_ff_2 (
    .S(\开始 ), .clk(CLK), .R(1'b0), .Qn(s_r_ff_2_qn), .reset(not_2_out));  // open: Q, preset
  Multiplexer #(.select(1), .width(1), .disabled("Z"), .enable("false")) multiplexer_1 (
    .in0(and_3_out), .in1(1'b1), .out(multiplexer_1_out), .sel(and_2_out));
  or or_1 (or_1_out, multiplexer_1_out, s_r_ff_2_qn);
  and and_4 (\对应的灯 , EN, or_1_out);

  // Notes on the sheet:
  //   本质就是一个计时器，断电的同时清零
  //   EN = 1，保持记忆状态，断电自动清零
  //   32Hz：3*60*32 = 1680(十六进制)
  //   状态记录，记录是否已经开始过
  //   已经开始过的保持为0，未开始国保持为1
  //   模块完成的标志信号
endmodule

module \洗衣流程控制  (
  input  \置1 ,
  input  MODE,
  input  \模式选择中 ,
  output [5:0] out_4,
  output [3:0] out_5,
  output [3:0] out_6
);

  wire and_1_out, n0, n1, n2, \洗衣流程控制组合电路_1_n0 , \洗衣流程控制组合电路_1_n1 , \洗衣流程控制组合电路_1_n2 ;

  \洗衣流程控制组合电路  \u_洗衣流程控制组合电路_1  (
    .S2(n2), .S1(n1), .S0(n0), .N2(\洗衣流程控制组合电路_1_n2 ), .N1(\洗衣流程控制组合电路_1_n1 ), .N0(\洗衣流程控制组合电路_1_n0 ));
  and and_1 (and_1_out, MODE, \模式选择中 );
  D_Flip_Flop #(.trigger("rising"), .Pre_Clr_Positions("ABOVE_BELOW"), .NegatePresetClear("false"), .enable("false"), .NewFFLayout("true")) d_ff_1 (
    .clk(and_1_out), .D(\洗衣流程控制组合电路_1_n2 ), .Q(n2), .preset(\置1 ));  // open: Qn, reset
  D_Flip_Flop #(.trigger("rising"), .Pre_Clr_Positions("ABOVE_BELOW"), .NegatePresetClear("false"), .enable("false"), .NewFFLayout("true")) d_ff_2 (
    .clk(and_1_out), .D(\洗衣流程控制组合电路_1_n1 ), .Q(n1), .preset(\置1 ));  // open: Qn, reset
  D_Flip_Flop #(.trigger("rising"), .Pre_Clr_Positions("ABOVE_BELOW"), .NegatePresetClear("false"), .enable("false"), .NewFFLayout("true")) d_ff_3 (
    .clk(and_1_out), .D(\洗衣流程控制组合电路_1_n0 ), .Q(n0), .preset(\置1 ));  // open: Qn, reset
  Multiplexer #(.select(3), .width(8), .disabled("Z"), .enable("false")) multiplexer_1 (
    .in0({8{1'b1}}), .in1(8'h30), .in2(8'h60), .in3(8'h90), .in4(8'h50), .in6(8'h11), .in7(8'h41),
    .out({out_6, out_5}), .sel({n2, n1, n0}));  // open: in5
  \洗衣流程控制输出函数  \u_洗衣流程控制输出函数_1  (
    .a(n2), .b(n1), .c(n0), .x(out_4[0]), .y(out_4[1]), .z(out_4[2]), .u(out_4[3]), .v(out_4[4]), .w(out_4[5]));

  // Notes on the sheet:
  //   设计一个Moore型电路
endmodule

module \漂洗模块  (
  input  EN,
  input  \开始 ,
  input  CLK,
  input  \暂停 ,
  output out_5,
  output \对应的灯 
);

  wire and_1_out, and_2_out, and_3_out, multiplexer_1_out, not_1_out, not_2_out, or_1_out,
       programmablegenerator_1_p1, s_r_ff_1_q, s_r_ff_2_qn, t_ff_1_q;

  T_Flip_Flop #(.trigger("rising"), .Pre_Clr_Positions("ABOVE_BELOW"), .NegatePresetClear("false"), .enable("false"), .NewFFLayout("true")) t_ff_1 (
    .clk(\暂停 ), .T(1'b1), .Q(t_ff_1_q), .reset(not_2_out));  // open: Qn, preset
  S_R_Flip_Flop #(.trigger("rising"), .Pre_Clr_Positions("ABOVE_BELOW"), .NegatePresetClear("false"), .enable("false"), .NewFFLayout("true")) s_r_ff_1 (
    .S(\开始 ), .clk(CLK), .R(out_5), .Q(s_r_ff_1_q), .reset(not_2_out));  // open: Qn, preset
  not not_1 (not_1_out, t_ff_1_q);
  not not_2 (not_2_out, EN);
  and and_1 (and_1_out, EN, s_r_ff_1_q, not_1_out);
  Counter #(.width(16), .max('h180), .ongoal("wrap"), .trigger("rising"), .behavior("new")) counter_1 (
    .count(and_1_out), .carry(out_5), .clk(CLK));  // open: load, D, Q, clr, preset, down
  and and_2 (and_2_out, t_ff_1_q, s_r_ff_1_q);
  // ProgrammableGenerator #(.nState(1), .Contents("10 10")) programmablegenerator_1: pin names not known; wires that end beside it: programmablegenerator_1_p1
  and and_3 (and_3_out, and_1_out, programmablegenerator_1_p1);
  S_R_Flip_Flop #(.trigger("rising"), .Pre_Clr_Positions("ABOVE_BELOW"), .NegatePresetClear("false"), .enable("false"), .NewFFLayout("true")) s_r_ff_2 (
    .S(\开始 ), .clk(CLK), .R(1'b0), .Qn(s_r_ff_2_qn), .reset(not_2_out));  // open: Q, preset
  Multiplexer #(.select(1), .width(1), .disabled("Z"), .enable("false")) multiplexer_1 (
    .in0(and_3_out), .in1(1'b1), .out(multiplexer_1_out), .sel(and_2_out));
  or or_1 (or_1_out, multiplexer_1_out, s_r_ff_2_qn);
  and and_4 (\对应的灯 , EN, or_1_out);

  // Notes on the sheet:
  //   本质就是一个计时器，断电的同时清零
  //   EN = 1，保持记忆状态，断电自动清零
  //   32Hz：3*60*32 = 
  //   状态记录，记录是否已经开始过
  //   已经开始过的保持为0，未开始国保持为1
  //   模块完成的标志信号
endmodule

module \甩干模块  (
  input  EN,
  input  \开始 ,
  input  CLK,
  input  \暂停 ,
  output out_5,
  output \对应的灯 
);

  wire and_1_out, and_2_out, and_3_out, multiplexer_1_out, not_1_out, not_2_out, or_1_out,
       programmablegenerator_1_p1, s_r_ff_1_q, s_r_ff_2_qn, t_ff_1_q;

  T_Flip_Flop #(.trigger("rising"), .Pre_Clr_Positions("ABOVE_BELOW"), .NegatePresetClear("false"), .enable("false"), .NewFFLayout("true")) t_ff_1 (
    .clk(\暂停 ), .T(1'b1), .Q(t_ff_1_q), .reset(not_2_out));  // open: Qn, preset
  S_R_Flip_Flop #(.trigger("rising"), .Pre_Clr_Positions("ABOVE_BELOW"), .NegatePresetClear("false"), .enable("false"), .NewFFLayout("true")) s_r_ff_1 (
    .S(\开始 ), .clk(CLK), .R(out_5), .Q(s_r_ff_1_q), .reset(not_2_out));  // open: Qn, preset
  not not_1 (not_1_out, t_ff_1_q);
  not not_2 (not_2_out, EN);
  and and_1 (and_1_out, EN, s_r_ff_1_q, not_1_out);
  Counter #(.width(16), .max('hc0), .ongoal("wrap"), .trigger("rising"), .behavior("new")) counter_1 (
    .count(and_1_out), .carry(out_5), .clk(CLK));  // open: load, D, Q, clr, preset, down
  and and_2 (and_2_out, t_ff_1_q, s_r_ff_1_q);
  // ProgrammableGenerator #(.nState(1), .Contents("10 10")) programmablegenerator_1: pin names not known; wires that end beside it: programmablegenerator_1_p1
  and and_3 (and_3_out, and_1_out, programmablegenerator_1_p1);
  S_R_Flip_Flop #(.trigger("rising"), .Pre_Clr_Positions("ABOVE_BELOW"), .NegatePresetClear("false"), .enable("false"), .NewFFLayout("true")) s_r_ff_2 (
    .S(\开始 ), .clk(CLK), .R(1'b0), .Qn(s_r_ff_2_qn), .reset(not_2_out));  // open: Q, preset
  Multiplexer #(.select(1), .width(1), .disabled("Z"), .enable("false")) multiplexer_1 (
    .in0(and_3_out), .in1(1'b1), .out(multiplexer_1_out), .sel(and_2_out));
  or or_1 (or_1_out, multiplexer_1_out, s_r_ff_2_qn);
  and and_4 (\对应的灯 , EN, or_1_out);

  // Notes on the sheet:
  //   本质就是一个计时器，断电的同时清零
  //   EN = 1，保持记忆状态，断电自动清零
  //   32Hz：3*60*32 = 
  //   状态记录，记录是否已经开始过
  //   已经开始过的保持为0，未开始国保持为1
  //   模块完成的标志信号
endmodule
